# Fritzing sketch MeasCentral (saved by Fritzing 1.0.4)
breadboards: 1

parts:
  MH-ET_LIVE_ESP32_DEVKIT1 = MH-ET LIVE ESP32 DEVKIT 38 pins
  GLCD_128x1 = 128 x 64 Graphic LCD
  DS1 = DS18B20 1-Wire Temperature Sensor [part_number=DS18B20]
  R1 = Resistor [tolerance=±5% power=0.25W resistance=220 package=THT]
  R2 = Resistor [tolerance=±5% power=0.25W resistance=220 package=THT]

nets:
  3V3: MH-ET_LIVE_ESP32_DEVKIT1.3V3, DS1.VDD, R2.Pin_0
  N1: MH-ET_LIVE_ESP32_DEVKIT1.GND#58, GLCD_128x1.1_Vss, GLCD_128x1.15_CS1, GLCD_128x1.20_K(-)
  N2: MH-ET_LIVE_ESP32_DEVKIT1.5V, GLCD_128x1.2_Vdd, R1.Pin_0
  N3: MH-ET_LIVE_ESP32_DEVKIT1.GND#64, DS1.GND
  N4: MH-ET_LIVE_ESP32_DEVKIT1.IO23, GLCD_128x1.5_R/W
  N5: MH-ET_LIVE_ESP32_DEVKIT1.IO22, GLCD_128x1.17_RST
  N6: MH-ET_LIVE_ESP32_DEVKIT1.IO18, GLCD_128x1.6_Enable
  N7: MH-ET_LIVE_ESP32_DEVKIT1.IO5, GLCD_128x1.4_D/I
  N8: MH-ET_LIVE_ESP32_DEVKIT1.IO15, DS1.DQ, R2.Pin_1
  N9: GLCD_128x1.19_A(+), R1.Pin_1

custom parts:
  MH-ET LIVE ESP32 DEVKIT 38 pins: http://mh.nodebb.com/topic/2/mh-et-live-esp32-devkit
